# Fritzing sketch ECC3313_Car (saved by Fritzing 0.9.10b)
breadboards: 1

parts:
  元件3 = Arduino Uno (Rev3)
  Part4 = Bluetooth HC-05 Macho
  S4 = 直流电机驱动模块L298N【红色】
  元件4 = 超声波测距传感器模块HC-SR04
  VCC2 = Battery block 9V
  Mod3 = 蜂鸣器 [package="Breakout board"]
  U2 = WS2812 RGB LED strip
  Buck_Convertor2 = Buck Convertor [part_number=LM2596 package=THT]
  M5 = DC Motor [voltage_(max)=6V voltage_(min)=3V]
  M6 = DC Motor [voltage_(max)=6V voltage_(min)=3V]
  M8 = DC Motor [voltage_(max)=6V voltage_(min)=3V]
  M9 = DC Motor [voltage_(max)=6V voltage_(min)=3V]
  元件5 = BH1750 光强度光照度传感器模块

nets:
  N1: 元件3.A1, Mod3.S
  GND: 元件3.A2, 元件3.GND, S4.GND, 元件4.GND, VCC2.-, Mod3.-, U2.GND, U2.DIN, Buck_Convertor2.Negative_Input, 元件5.GND
  N2: 元件3.A4/SDA, 元件5.SDA
  N3: 元件3.A5/SCL, 元件5.SCL
  N4: 元件3.D10_PWM/SS, S4.IN3
  N5: 元件3.D11_PWM/MOSI, S4.IN4
  N6: 元件3.D12/MISO, 元件4.Trig
  N7: 元件3.D13/SCK, 元件4.Echo
  N8: 元件3.D0/RX, Part4.RXD
  N9: 元件3.D1/TX, Part4.TXD
  N10: 元件3.D5_PWM, S4.IN1
  N11: 元件3.D6_PWM, S4.IN2
  3V3: 元件3.3V3, 元件5.VCC
  5V: 元件3.5V, S4.5V, 元件4.VCC, VCC2.+, Mod3.NC, U2.VCC, Buck_Convertor2.Positive_Input
  N12: Part4.VCC, Buck_Convertor2.Positive_Output
  N13: Part4.GND, Buck_Convertor2.Negative_Output
  N14: S4.M1-01, M6.pin_2, M8.pin_2
  N15: S4.M1-02, M6.pin_1, M8.pin_1
  N16: S4.M2-01, M5.pin_2
  N17: S4.M2-02, M5.pin_1, M9.pin_1

notes:
  5v LED
  5v ultrasonic sensor
  3.3v HC-05 bluetooth
  5v WS2812B LED
  7v L298N_LEFT
  5v buzzer
  3.3v IR sensor-LIGHT SENSOR
  7v power 18650 - 2
  fixed 3.3v- BUCK for HC05
  DC motor_BACK
  fixed 5v- BUCK for Power
  CHEN JUNXU
  HAZEEQ
  AMAR
  LIU HAO

custom parts:
  Arduino Uno (Rev3): The Arduino Uno is a microcontroller board based on the ATmega328 (datasheet). It has 14 digital input/output pins (of which 6 can be used as PWM outputs), 6 analog inputs, a 16 MHz ceramic resonator, a USB connection, a power jack, an ICSP header, and a reset button. It contains everything needed to support the microcontroller; simply connect it to a computer with a USB cable or power it with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
  直流电机驱动模块L298N【红色】: h-bridge
  蜂鸣器: Active Piezoelectric Buzzer Module KY-012, it produces single-tone sound when signal is high. (Special thanks to vanepp for fixing the PCB holes and other errors)
  WS2812 RGB LED strip: WS2812 strip
  Buck Convertor: DC to DC buck convertor
  BH1750 光强度光照度传感器模块: Light Sensor
